// Logisim project processor.circ as structural Verilog
module program_counter (
  input  enable,
  input  clock,
  input  reset,
  output [7:0] address
);

  wire [7:0] adder_1_out;

  Register register_1 (.D(adder_1_out), .en(enable), .clk(clock), .Q(address), .clr(reset));
  Adder adder_1 (.a(8'h1), .b(address), .out(adder_1_out));  // open: cin, cout
endmodule

module monocycle_processor (
  input  reset,
  input  in_2,
  output [7:0] out_3,
  output [31:0] out_4
);

  wire clock_1_out;

  Clock clock_1 (.out(clock_1_out));
  ROM #(.dataWidth(32)) rom_1 (.addr(out_3), .data(out_4));
  program_counter program_counter_1 (.enable(in_2), .clock(clock_1_out), .reset(reset), .address(out_3));

  // Notes on the sheet:
  //   contents of rom_1 (hex, n*v repeats v):
  //   8*0 4
endmodule
